# Fritzing sketch Elpanna (saved by Fritzing 0.8.3b)
circuit board: 6.88561cm x 5.36311cm
breadboards: 1

parts:
  R3 = Resistor [tolerance=±5% resistance=10k package=THT]
  IC1 = ULN2803A [package=THT]
  J1 = shrouded pin header, 34 pins [form="♂ (shrouded male)"]
  R4 = Resistor [tolerance=±5% resistance=120 package=THT]
  SW1 = DIP SWITCH [package=dipswitch-02]
  C2 = Electrolytic Capacitor [capacitance=1µF package="100 mil [THT, electrolytic]"]
  Arduino1 = Arduino Uno (Rev3)
  R2 = Resistor [tolerance=±5% resistance=220 package=THT]
  LED2 = LED - 5mm [color="Green (570nm)" package="5 mm [THT]"]
  R1 = Resistor [tolerance=±5% resistance=220 package=THT]
  LED1 = LED - 5mm [color="Red (633nm)" package="5 mm [THT]"]
  SW2 = DIP SWITCH [package=dipswitch-02]  # not connected
  Raspberry_Pi_rev1 = Raspberry Pi rev2
  Q1 = NPN-Transistor [package="TO92 [THT]"]
  C3 = Electrolytic Capacitor [capacitance=1µF package="100 mil [THT, electrolytic]"]

nets:
  GND: R3.Pin_0, IC1.0V, J1.pin17, C2.+, Arduino1.GND, R2.Pin_1, R1.Pin_1, Raspberry_Pi_rev1.GND, C3.+
  N1: R3.Pin_1, J1.pin1, Arduino1.A0
  N2: IC1.In_1, Arduino1.D2
  N3: IC1.In_2, Arduino1.D3_PWM
  N4: IC1.In_3, Arduino1.D4
  N5: IC1.In_4, Arduino1.D5_PWM
  N6: IC1.In_5, Arduino1.D6_PWM
  N7: IC1.In_6, Arduino1.D7
  N8: IC1.In_7, Arduino1.D8
  N9: IC1.In_8, Arduino1.D9_PWM
  N10: IC1.COM_-_Common, J1.pin16
  N11: IC1.Out_8, J1.pin10
  N12: IC1.Out_7, J1.pin9
  N13: IC1.Out_6, J1.pin8
  N14: IC1.Out_5, J1.pin7
  N15: IC1.Out_4, J1.pin6
  N16: IC1.Out_3, J1.pin5
  N17: IC1.Out_2, J1.pin4
  N18: IC1.Out_1, J1.pin3
  N19: J1.pin2, Arduino1.VIN
  N20: J1.pin34, R4.Pin_0, Arduino1.5V
  N21: R4.Pin_1, SW1.1
  N22: SW1.2, C2.-
  N23: SW1.3, SW1.4, Arduino1.RESET
  N24: Arduino1.D12/MISO, LED2.anode
  N25: Arduino1.D13/SCK, LED1.anode
  N26: R2.Pin_0, LED1.cathode
  N27: LED2.cathode, R1.Pin_0
  N28: Raspberry_Pi_rev1.GPIO_23, Q1.B

notes:
  Enable and disable autoreset on serial port connection
  Resistor for Diecimila board
  Should be 110 < Ohm < 124
  Capacitor for Uno board
  Should be 10uF (100uF works too)
  playground.arduino.cc/Main/DisablingAutoResetOnSerialConnection
  This is not doing anything, I only had a 4 pin DIP
  This section is only an idea and not yet implemented
